# Fritzing sketch schematic_old (saved by Fritzing 0.9.3b)
circuit board: 8.46667cm x 5.64444cm
breadboards: 1

parts:
  R1 = Resistor [tolerance=±5% resistance=1k package=THT]
  R2 = Resistor [tolerance=±5% resistance=1k package=THT]
  C1 = Ceramic Capacitor [capacitance=100nF package="100 mil [THT, multilayer]"]
  R3 = Resistor [tolerance=±5% resistance=1k package=THT]
  R4 = Resistor [tolerance=±5% resistance=1k package=THT]
  C2 = Ceramic Capacitor [capacitance=100nF package="100 mil [THT, multilayer]"]
  J1_(Meters) = male pin header, 4 pins [form="♂ (male)"]
  R5 = Resistor [tolerance=±5% resistance=5.6k package=THT]
  R6 = Resistor [tolerance=±5% resistance=2.2k package=THT]
  S1 = Pushbutton [package=THT]
  J3_(Meters) = female pin header, 4 pins [form="♀ (female)"]
  R7 = Resistor [tolerance=±5% resistance=2.2k package=THT]
  R8 = Resistor [tolerance=±5% resistance=5.6k package=THT]
  S2 = Pushbutton [package=THT]
  J2_(Arduino) = male pin header, 4 pins [form="♂ (male)"]

nets:
  N1: R1.Pin_0, R2.Pin_1
  5V: R1.Pin_1, R4.Pin_1, J2_(Arduino).pin1
  N2: R2.Pin_0, C1.1, J2_(Arduino).pin3
  GND: C1.0, J1_(Meters).pin4, R5.Pin_0, R6.Pin_0, J3_(Meters).pin4, R7.Pin_0, R8.Pin_0, J2_(Arduino).pin4
  N3: R3.Pin_0, C2.1, J2_(Arduino).pin2
  N4: R3.Pin_1, R4.Pin_0, J1_(Meters).pin2
  N5: R5.Pin_1, S1.leg1, J3_(Meters).pin1
  N6: R6.Pin_1, S1.leg0
  N7: J3_(Meters).pin2, R8.Pin_1, S2.leg1
  N8: R7.Pin_1, S2.leg0
